# Fritzing sketch EUFY remote control (saved by Fritzing 0.9.3b)

parts:
  U1 = NodeMCU V1.0
  IR1 = TSOP312.., 314.. [package=THT]
  USBTTL1 = USB TTL Serial Cable
  D1 = LTE-302 [package=lte-302]  # not connected

nets:
  N1: U1.D1, IR1.Data
  N2: U1.3V3, IR1.Vs
  GND: U1.GND, IR1.GND, USBTTL1.GND
  VIN: U1.Vin, USBTTL1.5V

notes:
  Power using micro USB
  IR LED
  IR Reciever

custom parts:
  NodeMCU V1.0: ESP8266 based NodeMCU
