# Fritzing sketch EUFY remote read (saved by Fritzing 0.9.3b)

parts:
  IR2 = TSOP312.., 314.. [package=THT]
  Part1 = Arduino Uno (Rev3)

nets:
  N1: IR2.GND, Part1.D2
  N2: IR2.Vs, Part1.GND
  N3: IR2.Data, Part1.3V3
